// Logisim project BASIC GATES.circ as structural Verilog
module main (
  input  in_1,
  input  in_2,
  input  in_3,
  input  in_4,
  input  in_5,
  input  in_6,
  input  in_7,
  input  in_8,
  output out_9,
  output out_10,
  output out_11,
  output out_12
);

  wire transistor_3_out, transistor_10_out, transistor_11_out, transistor_13_out;

  Transistor transistor_1 (.in(1'b0), .out(out_12), .gate(in_5));
  Transistor #(.\type ("n")) transistor_2 (.in(1'b1), .out(out_10), .gate(in_1));
  Transistor #(.\type ("n")) transistor_3 (.in(1'b1), .out(transistor_3_out), .gate(in_5));
  Transistor #(.\type ("n")) transistor_4 (.in(transistor_3_out), .out(out_12), .gate(in_7));
  Transistor transistor_5 (.in(1'b0), .out(out_12), .gate(in_7));
  Transistor #(.\type ("n")) transistor_6 (.in(1'b1), .out(out_10), .gate(in_4));
  Transistor transistor_7 (.in(1'b1), .out(out_11), .gate(in_6));
  Transistor transistor_8 (.in(1'b1), .out(out_11), .gate(in_8));
  Transistor #(.\type ("n")) transistor_9 (.in(transistor_10_out), .out(out_11), .gate(in_6));
  Transistor #(.\type ("n")) transistor_10 (.in(1'b0), .out(transistor_10_out), .gate(in_8));
  Transistor transistor_11 (.in(1'b1), .out(transistor_11_out), .gate(in_2));
  Transistor transistor_12 (.in(transistor_11_out), .out(out_9), .gate(in_3));
  Transistor #(.\type ("n")) transistor_13 (.in(out_9), .out(transistor_13_out), .gate(in_2));
  Transistor #(.\type ("n")) transistor_14 (.in(out_9), .out(transistor_13_out), .gate(in_3));
  // also tied to GND on the sheet: transistor_13_out
endmodule
